# Fritzing sketch Big power supply (PSU) (saved by Fritzing 0.9.10b)
circuit board: 12.3896cm x 6.096cm
breadboards: 1

parts:
  D1 = Rectifier Diode [part_number=1N4001 package="300 mil [THT]"]
  D2 = Rectifier Diode [part_number=1N4001 package="300 mil [THT]"]
  D3 = Rectifier Diode [part_number=1N4001 package="300 mil [THT]"]
  D4 = Rectifier Diode [part_number=1N4001 package="300 mil [THT]"]
  7805CT = Voltage Regulator - 5V [package="TO220 [THT]"]
  Fuse = Fuse with Handler [part_number=Htc-15m]
  R1 = Rotary Potentiometer (Large) [maximum_resistance=10kΩ knob_status=50% power=0.5W package=THT]
  Transformer = Transformer [package=transformer]
  LED1 = LED - 5mm [color="Red (633nm)" current=0.030 package="5 mm [THT]"]
  R3 = Resistor [tolerance=±5% power=0.25 resistance=220 package=THT]
  Gnd = BANANA_CONN [package=banana_conn]
  +5v = BANANA_CONN [package=banana_conn]
  +_Adjustable = BANANA_CONN [package=banana_conn]
  Gnd_2 = BANANA_CONN [package=banana_conn]
  LM317K = LM317K Voltage Regulator
  Power_plug = Power plug
  S1 = Taiway 100-SP-X-T1 SPDT Miniature Toggle Switch [part_number=100-SP-X-T1-0-0-B1-M1 package=THT]
  C1 = Electrolytic Capacitor [capacitance=2.2mF voltage=0.1kV package="300 mil [THT, electrolytic]"]
  C2 = Electrolytic Capacitor [capacitance=2.2mF voltage=35V package="300 mil [THT, electrolytic]"]
  R2 = Resistor [tolerance=±5% power=0.25W resistance=220 package=THT]
  C3 = Tantalum Capacitor [capacitance=0.1µF voltage=35V package="100 mil [THT, tantalum]"]

nets:
  N1: D1.cathode, D3.anode, Transformer.3
  GND: D1.anode, D4.anode, 7805CT.GND, R1.wiper, LED1.cathode, Gnd.1, Gnd_2.1, C1.-, C2.-, C3.-
  N2: D2.cathode, D3.cathode, 7805CT.input_voltage, LM317K.Input, C1.+, C2.+
  N3: D2.anode, D4.cathode, Transformer.4
  N4: 7805CT.output_voltage, R3.Pin_1, +5v.1
  N5: Fuse.Connector1, S1.L1
  N6: Fuse.Connector2, Transformer.1
  N7: R1.leg1, LM317K.Adjust, R2.Pin_1
  N8: Transformer.2, Power_plug.GND
  N9: LED1.anode, R3.Pin_0
  N10: +_Adjustable.1, LM317K.Output, R2.Pin_0, C3.+
  N11: Power_plug.VCC, S1.COM

custom parts:
  LM317K Voltage Regulator: LM317K voltage regulator in TO3 package. Based on the MJ11016 by Peter Van Epp (vanepp in forums). Changes: pin names, metadata, output connector from male to pad.
